# Fritzing sketch water_level_circuit (saved by Fritzing 1.0.2b)
breadboards: 1

parts:
  M1 = DOIT Esp32 DevKit v1 (30 pins long, 11 pins width) [part_number=ESP32S-PIN30]
  HC-SR04_Sensor_1 = HC-SR04 Ultrasonic Distance Sensor
  J1 = Basic Servo
  J2 = Basic Servo

nets:
  GND: M1.GND, HC-SR04_Sensor_1.GND, J1.gnd, J2.gnd
  N1: M1.D26, J2.vcc
  N2: M1.D27, J1.vcc
  N3: M1.D12, HC-SR04_Sensor_1.ECHO
  N4: M1.D13, HC-SR04_Sensor_1.TRIG
  VIN: M1.VIN, HC-SR04_Sensor_1.VCC, J1.pulse, J2.pulse

notes:
  Ultrasonic Sensor
  Water Pump Servo
  Draining Servo

custom parts:
  DOIT Esp32 DevKit v1 (30 pins long, 11 pins width): The DOIT Esp32 DevKit v1 is one of the development board created by DOIT to evaluate the ESP-WROOM-32 module. It is based on the ESP32 microcontroller that boasts Wifi, Bluetooth, Ethernet and Low Power support all in a single chip. (vanepp) made breadboard work, adjusted pin numbering and labels and reduced size of schematic and cleaned up pcb. This chip is 30pins long (2 x15) and 11 pins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
